# Fritzing sketch Dual_OTA_VCA_V-I_Convert_Test (saved by Fritzing 0.9.3b)
breadboards: 1

parts:
  R2 = TRIMPOT [package=3362u-2]
  IC1 = Dual Op-Amp [package=dip08]
  R3 = TRIMPOT [package=3362u-2]
  C1 = Film/Foil Capacitor [capacitance=100nF voltage=35V package="5mm [THT, pp]"]
  IC2 = Dual Op-Amp [package=dip08]
  IC3 = Dual Op-Amp [package=dip08]
  R4 = Resistor [tolerance=±5% resistance=10k package=THT]
  R5 = Resistor [tolerance=±5% resistance=1k package=THT]
  Q1 = PNP-Transistor [package="TO92 [THT]"]
  C2 = Ceramic Capacitor [capacitance=100nF package="100 mil [THT, multilayer]"]
  C3 = Ceramic Capacitor [capacitance=100nF package="100 mil [THT, multilayer]"]
  C4 = Ceramic Capacitor [capacitance=100nF package="100 mil [THT, multilayer]"]
  C5 = Ceramic Capacitor [capacitance=100nF package="100 mil [THT, multilayer]"]
  C6 = Ceramic Capacitor [capacitance=100nF package="100 mil [THT, multilayer]"]
  C7 = Ceramic Capacitor [capacitance=100nF package="100 mil [THT, multilayer]"]
  C12 = Ceramic Capacitor [capacitance=100nF package="100 mil [THT, multilayer]"]
  R6 = Resistor [tolerance=±5% resistance=10k package=THT]

nets:
  N1: R2.CCW, IC1.B_+IN, C1.+, IC2.B_+IN, IC3.A_+IN, IC3.B_+IN, C2.0, C3.0, C4.0, C5.1, C6.1, C7.1, R6.Pin_1
  N2: R2.WIPER, IC1.A_+IN
  N3: IC1.A_OUT, IC1.A_-IN, R3.CCW, R3.WIPER
  N4: IC1.A_V-, IC2.A_V-, IC3.A_V-, C5.0, C6.0, C7.0
  N5: IC1.B_-IN, IC1.B_OUT
  N6: IC1.A_V+, IC2.A_V+, IC3.A_V+, C2.1, C3.1, C4.1
  N7: R3.CW, C1.-, IC2.A_+IN
  N8: IC2.A_OUT, IC2.A_-IN, R4.Pin_0
  N9: IC2.B_-IN, IC2.B_OUT
  N10: IC3.A_OUT, Q1.C, C12.1
  N11: IC3.A_-IN, R4.Pin_1, R5.Pin_0, C12.0
  N12: IC3.B_-IN, IC3.B_OUT
  N13: R5.Pin_1, Q1.E
  N14: Q1.B, R6.Pin_0

notes:
  GND
  +5V
  -5V
  GND
  Envelope Generator
  +3.3Vp-p
  4Hz
  VOUT
