# Fritzing sketch Dual_OTA_VCA_VCCS_Unit_Test (saved by Fritzing 0.9.3b)
breadboards: 1
perfboards: 1

parts:
  R6 = Resistor [tolerance=±5% resistance=82k package=THT]
  R7 = TRIMPOT [package=3362u-2]
  C8 = Electrolytic Capacitor [capacitance=1µF package="100 mil [THT, electrolytic]"]
  R8 = Resistor [tolerance=±5% resistance=47k package=THT]
  IC4 = IC, DIP package, 16 pins [chip_label=NJM13600]
  R9 = Resistor [tolerance=±5% resistance=33k package=THT]
  C9 = Ceramic Capacitor [capacitance=100nF package="100 mil [THT, multilayer]"]
  R10 = Resistor [tolerance=±5% resistance=4.7k package=THT]
  C10 = Electrolytic Capacitor [capacitance=1µF package="100 mil [THT, electrolytic]"]
  R11 = Resistor [tolerance=±5% resistance=100k package=THT]
  C11 = Ceramic Capacitor [capacitance=100nF package="100 mil [THT, multilayer]"]
  J1 = STM32 Nucleo boards  # not connected

nets:
  N1: R6.Pin_1, R7.CW
  N2: R7.CCW, R8.Pin_1, IC4.pin4, IC4.pin14, R9.Pin_1, C9.0, R11.Pin_1, C11.0
  N3: R7.WIPER, C8.+
  N4: C8.-, R8.Pin_0, IC4.pin3
  N5: IC4.pin5, IC4.pin7, R9.Pin_0
  N6: IC4.pin6, C9.1, R10.Pin_1
  N7: IC4.pin8, R10.Pin_0, C10.-
  N8: IC4.pin10, IC4.pin12, IC4.pin13
  N9: IC4.pin11, C11.1
  N10: C10.+, R11.Pin_0

notes:
  -5V
  GND
  NJM13700
  1 AMP BIAS INPUT A 16 AMP BIAS INPUT B
  2 DIODE BIAS A 15 DIODE BIAS B
  3 +INPUT A 14 +INPUT B
  4 -INPUT A 13 -INPUT B
  5 OUTPUT A 12 OUTPUT B
  6 V- 11 V+
  7 BUFFER INPUT A 10 BUFFER INPUT B
  8 BUFFER OUTPUT A 9 BUFFER OUTPUT B
  GND
  +5V
  Wave Out
  Wave In
  Envelope
  VCCS Unit
  Envelope(V)
  +3.3Vp-p Saw
