# Fritzing sketch Dual_OTA_VCA_ch_Test (saved by Fritzing 0.9.3b)
breadboards: 2

parts:
  R2 = TRIMPOT [package=3362u-2]
  IC1 = Dual Op-Amp [package=dip08]
  R3 = TRIMPOT [package=3362u-2]
  C1 = Film/Foil Capacitor [capacitance=100nF voltage=35V package="5mm [THT, pp]"]
  IC2 = Dual Op-Amp [package=dip08]
  IC3 = Dual Op-Amp [package=dip08]
  R4 = Resistor [tolerance=±5% resistance=10k package=THT]
  R5 = Resistor [tolerance=±5% resistance=1k package=THT]
  Q1 = PNP-Transistor [package="TO92 [THT]"]
  C2 = Ceramic Capacitor [capacitance=100nF package="100 mil [THT, multilayer]"]
  C3 = Ceramic Capacitor [capacitance=100nF package="100 mil [THT, multilayer]"]
  C4 = Ceramic Capacitor [capacitance=100nF package="100 mil [THT, multilayer]"]
  C5 = Ceramic Capacitor [capacitance=100nF package="100 mil [THT, multilayer]"]
  C6 = Ceramic Capacitor [capacitance=100nF package="100 mil [THT, multilayer]"]
  C7 = Ceramic Capacitor [capacitance=100nF package="100 mil [THT, multilayer]"]
  R6 = Resistor [tolerance=±5% resistance=82k package=THT]
  R7 = TRIMPOT [package=3362u-2]
  C8 = Electrolytic Capacitor [capacitance=1µF package="100 mil [THT, electrolytic]"]
  R8 = Resistor [tolerance=±5% resistance=47k package=THT]
  IC4 = IC, DIP package, 16 pins [chip_label=NJM13600]
  R9 = Resistor [tolerance=±5% resistance=33k package=THT]
  C9 = Ceramic Capacitor [capacitance=100nF package="100 mil [THT, multilayer]"]
  R10 = Resistor [tolerance=±5% resistance=4.7k package=THT]
  C10 = Electrolytic Capacitor [capacitance=1µF package="100 mil [THT, electrolytic]"]
  R11 = Resistor [tolerance=±5% resistance=100k package=THT]
  C11 = Ceramic Capacitor [capacitance=100nF package="100 mil [THT, multilayer]"]
  C12 = Ceramic Capacitor [capacitance=100nF package="100 mil [THT, multilayer]"]
  R12 = TRIMPOT [package=3362u-2]
  R13 = TRIMPOT [package=3362u-2]
  C13 = Film/Foil Capacitor [capacitance=100nF voltage=35V package="5mm [THT, pp]"]
  R14 = Resistor [tolerance=±5% resistance=10k package=THT]
  R15 = Resistor [tolerance=±5% resistance=1k package=THT]
  Q2 = PNP-Transistor [package="TO92 [THT]"]
  LED1 = LED - 5mm [color="Green (565nm)" package="5 mm [THT]"]
  R16 = Resistor [tolerance=±5% resistance=10k package=THT]
  C14 = Electrolytic Capacitor [capacitance=1µF package="100 mil [THT, electrolytic]"]
  C15 = Electrolytic Capacitor [capacitance=1µF package="100 mil [THT, electrolytic]"]
  C16 = Electrolytic Capacitor [capacitance=1µF package="100 mil [THT, electrolytic]"]
  R17 = Resistor [tolerance=±5% resistance=100k package=THT]
  R18 = Resistor [tolerance=±5% resistance=4.7k package=THT]
  R19 = Resistor [tolerance=±5% resistance=33k package=THT]
  C17 = Electrolytic Capacitor [capacitance=1µF package="100 mil [THT, electrolytic]"]
  R20 = Resistor [tolerance=±5% resistance=47k package=THT]
  R21 = TRIMPOT [package=3362u-2]
  R22 = Resistor [tolerance=±5% resistance=82k package=THT]

nets:
  N1: R2.CCW, C1.+, IC3.A_+IN, IC3.B_+IN, C2.1, C3.1, C4.1, C5.1, C6.1, C7.1, R7.CCW, R8.Pin_1, IC4.pin4, IC4.pin13, R9.Pin_1, C9.0, R11.Pin_1, C11.1, R12.CCW, C13.-, C14.-, C15.+, R17.Pin_0, R19.Pin_0, R20.Pin_0, R21.CCW
  N2: R2.WIPER, IC1.A_+IN
  N3: R2.CW, R12.CW
  N4: IC1.A_OUT, IC1.A_-IN, R3.CCW, R3.WIPER
  N5: IC1.A_V-, IC2.A_V-, IC3.A_V-, C5.0, C6.0, C7.0, IC4.pin6, C9.1, R10.Pin_1, R16.Pin_1, C15.-, R18.Pin_0
  N6: IC1.B_+IN, R12.WIPER
  N7: IC1.B_-IN, IC1.B_OUT, R13.CCW, R13.WIPER
  N8: IC1.A_V+, IC2.A_V+, IC3.A_V+, C2.0, C3.0, C4.0, IC4.pin11, C11.0, LED1.anode, C14.+
  N9: R3.CW, C1.-, IC2.A_+IN
  N10: IC2.A_OUT, IC2.A_-IN, R4.Pin_0
  N11: IC2.B_+IN, R13.CW, C13.+
  N12: IC2.B_-IN, IC2.B_OUT, R14.Pin_0
  N13: IC3.A_OUT, Q1.C, C12.1
  N14: IC3.A_-IN, R4.Pin_1, R5.Pin_0, C12.0
  N15: IC3.B_-IN, R14.Pin_1, R15.Pin_0
  N16: IC3.B_OUT, Q2.C
  N17: R5.Pin_1, Q1.E
  N18: Q1.B, IC4.pin1
  N19: R6.Pin_0, R22.Pin_0
  N20: R6.Pin_1, R7.CW
  N21: R7.WIPER, C8.+
  N22: C8.-, R8.Pin_0, IC4.pin3
  N23: IC4.pin5, IC4.pin7, R9.Pin_0
  N24: IC4.pin8, R10.Pin_0, C10.-
  N25: IC4.pin9, C16.-, R18.Pin_1
  N26: IC4.pin10, IC4.pin12, R19.Pin_1
  N27: IC4.pin14, C17.-, R20.Pin_1
  N28: IC4.pin16, Q2.B
  N29: C10.+, R11.Pin_0
  N30: R15.Pin_1, Q2.E
  N31: LED1.cathode, R16.Pin_0
  N32: C16.+, R17.Pin_1
  N33: C17.+, R21.WIPER
  N34: R21.CW, R22.Pin_1

notes:
  GND
  +5V
  -5V
  GND
  Envelope Generator
  +3.3Vp-p
  4Hz
  NJM13700
  1 AMP BIAS INPUT A 16 AMP BIAS INPUT B
  2 DIODE BIAS A 15 DIODE BIAS B
  3 +INPUT A 14 +INPUT B
  4 -INPUT A 13 -INPUT B
  5 OUTPUT A 12 OUTPUT B
  6 V- 11 V+
  7 BUFFER INPUT A 10 BUFFER INPUT B
  8 BUFFER OUTPUT A 9 BUFFER OUTPUT B
  Wave Out A
  Wave In
  Envelope
  Wave Out B
