# Fritzing sketch OTA_VCA_BiasIN_2_Test (saved by Fritzing 0.9.3b)
breadboards: 1

parts:
  R1 = TRIMPOT [package=3362u-2]
  R2 = Resistor [tolerance=±5% resistance=330 package=THT]
  C1 = Film/Foil Capacitor [capacitance=100nF voltage=35V package="5mm [THT, pp]"]
  IC1 = Dual Op-Amp [package=dip08]
  R3 = TRIMPOT [package=3362u-2]
  Q1 = PNP-Transistor [package="TO92 [THT]"]
  R4 = Resistor [tolerance=±5% resistance=1k package=THT]
  C2 = Ceramic Capacitor [capacitance=100nF package="100 mil [THT, multilayer]"]
  C3 = Ceramic Capacitor [capacitance=100nF package="100 mil [THT, multilayer]"]

nets:
  N1: R1.WIPER, R1.CW, C1.-, IC1.B_+IN
  N2: R2.Pin_0, Q1.E
  N3: R2.Pin_1, IC1.A_-IN, R3.WIPER, R3.CW
  N4: C1.+, IC1.A_+IN, R4.Pin_1, C2.0, C3.1
  N5: IC1.A_OUT, Q1.C
  N6: IC1.A_V-, C3.0
  N7: IC1.B_-IN, IC1.B_OUT, R3.CCW
  N8: IC1.A_V+, C2.1
  N9: Q1.B, R4.Pin_0

notes:
  Saw wave Generator
  +1Vp-p
  1kHz
  -5V
  GND
  GND
  +5V
  1k Trim
  10k Trim
