# Fritzing sketch OTA_VCA_BiasIN_3_Test (saved by Fritzing 0.9.3b)
breadboards: 2

parts:
  R1 = TRIMPOT [package=3362u-2]
  R2 = Resistor [tolerance=±5% resistance=1k package=THT]
  C1 = Film/Foil Capacitor [capacitance=100nF voltage=35V package="5mm [THT, pp]"]
  IC1 = Dual Op-Amp [package=dip08]
  Q1 = PNP-Transistor [package="TO92 [THT]"]
  R4 = Resistor [tolerance=±5% resistance=1k package=THT]
  C2 = Ceramic Capacitor [capacitance=100nF package="100 mil [THT, multilayer]"]
  C3 = Ceramic Capacitor [capacitance=100nF package="100 mil [THT, multilayer]"]
  R5 = Resistor [tolerance=±5% resistance=10k package=THT]
  R7 = TRIMPOT [package=3362u-2]
  IC2 = Dual Op-Amp [package=dip08]
  C4 = Ceramic Capacitor [capacitance=100nF package="100 mil [THT, multilayer]"]
  C5 = Ceramic Capacitor [capacitance=100nF package="100 mil [THT, multilayer]"]
  C6 = Electrolytic Capacitor [capacitance=1µF package="100 mil [THT, electrolytic]"]
  C7 = Electrolytic Capacitor [capacitance=1µF package="100 mil [THT, electrolytic]"]
  R8 = Resistor [tolerance=±5% resistance=10k package=THT]
  C8 = Electrolytic Capacitor [capacitance=1µF package="100 mil [THT, electrolytic]"]
  C9 = Electrolytic Capacitor [capacitance=1µF package="100 mil [THT, electrolytic]"]

nets:
  N1: R1.CCW, IC2.B_-IN, IC2.B_OUT
  N2: R1.WIPER, R1.CW, C1.-, IC1.B_+IN
  N3: R2.Pin_0, Q1.E
  N4: R2.Pin_1, IC1.A_-IN, R5.Pin_1
  N5: C1.+, IC1.A_+IN, R4.Pin_1, C2.0, C3.1, R7.CCW, IC2.A_+IN, C4.0, C5.0, C6.-, C7.+, C8.-, C9.+
  N6: IC1.A_OUT, Q1.C
  N7: IC1.A_V-, C3.0, IC2.A_V-, C5.1, C7.-, C9.-
  N8: IC1.B_-IN, IC1.B_OUT, R5.Pin_0
  N9: IC1.A_V+, C2.1, IC2.A_V+, C4.1, C6.+, C8.+
  N10: Q1.B, R4.Pin_0
  N11: R7.WIPER, IC2.B_+IN
  N12: R7.CW, R8.Pin_0
  N13: IC2.A_OUT, IC2.A_-IN

notes:
  Envelope Generator
  +3.3Vp-p
  2kHz
  -5V
  GND
  GND
  +5V
  10k Trim
  100k Trim
