# Fritzing sketch OTA_VCA_BiasIN_4_Test (saved by Fritzing 0.9.3b)
breadboards: 1

parts:
  R1 = TRIMPOT [package=3362u-2]
  R2 = Resistor [tolerance=±5% resistance=1k package=THT]
  C1 = Film/Foil Capacitor [capacitance=100nF voltage=35V package="5mm [THT, pp]"]
  IC1 = Dual Op-Amp [package=dip08]
  Q1 = PNP-Transistor [package="TO92 [THT]"]
  R4 = Resistor [tolerance=±5% resistance=1k package=THT]
  C2 = Ceramic Capacitor [capacitance=100nF package="100 mil [THT, multilayer]"]
  C3 = Ceramic Capacitor [capacitance=100nF package="100 mil [THT, multilayer]"]
  R5 = Resistor [tolerance=±5% resistance=3.3k package=THT]
  IC2 = Dual Op-Amp [package=dip08]
  R7 = TRIMPOT [package=3362u-2]
  C6 = Ceramic Capacitor [capacitance=100nF package="100 mil [THT, multilayer]"]
  C7 = Ceramic Capacitor [capacitance=100nF package="100 mil [THT, multilayer]"]

nets:
  N1: R1.CCW, IC2.B_-IN, IC2.B_OUT
  N2: R1.WIPER, R1.CW, C1.-, IC1.B_+IN
  N3: R2.Pin_0, Q1.E
  N4: R2.Pin_1, IC1.A_-IN, R5.Pin_1
  N5: C1.+, IC1.A_+IN, C2.0, C3.1, IC2.A_V-, R7.CCW, C6.0, C7.0
  N6: IC1.A_OUT, Q1.C
  N7: IC1.A_V-, R4.Pin_1, C3.0, C7.1
  N8: IC1.B_-IN, IC1.B_OUT, R5.Pin_0
  N9: IC1.A_V+, C2.1, IC2.A_V+, C6.1
  N10: Q1.B, R4.Pin_0
  N11: IC2.A_-IN, IC2.A_+IN
  N12: IC2.B_+IN, R7.WIPER

notes:
  Envelope Generator
  +3.3Vp-p
  2kHz
  -5V
  GND
  GND
  +5V
  10k Trim
