# Fritzing sketch OTA_VCA_Nucleo_Test (saved by Fritzing 0.9.3b)
breadboards: 1
perfboards: 1

parts:
  IC1 = IC, DIP package, 16 pins [chip_label=NJM13700]
  R1 = Resistor [tolerance=±5% resistance=4.7k package=THT]
  R2 = Resistor [tolerance=±5% resistance=33k package=THT]
  C1 = Electrolytic Capacitor [capacitance=1µF package="100 mil [THT, electrolytic]"]
  R3 = Resistor [tolerance=±5% resistance=100k package=THT]
  C2 = Ceramic Capacitor [capacitance=100nF package="100 mil [THT, multilayer]"]
  C3 = Ceramic Capacitor [capacitance=100nF package="100 mil [THT, multilayer]"]
  VCC1 = Battery
  VCC2 = Battery
  J1 = STM32 Nucleo boards  # not connected

nets:
  N1: IC1.pin4, IC1.pin14, R2.Pin_1, C1.+, R3.Pin_0, R3.Pin_1, C2.0, C3.0, VCC1.-, VCC2.+
  N2: IC1.pin5, IC1.pin7, R2.Pin_0
  N3: IC1.pin6, R1.Pin_1, C2.1, VCC2.-
  N4: IC1.pin8, R1.Pin_0, C1.-
  N5: IC1.pin10, IC1.pin12, IC1.pin13
  N6: IC1.pin11, C3.1, VCC1.+

notes:
  NJM13700
  1 AMP BIAS INPUT A 16 AMP BIAS INPUT B
  2 DIODE BIAS A 15 DIODE BIAS B
  3 +INPUT A 14 +INPUT B
  4 -INPUT A 13 -INPUT B
  5 OUTPUT A 12 OUTPUT B
  6 V- 11 V+
  7 BUFFER INPUT A 10 BUFFER INPUT B
  8 BUFFER OUTPUT A 9 BUFFER OUTPUT B
  BIAS
  VCCS Unit
  WaveIn
  PCM5102A_FG
  +-500mVp-p
  Sine
  V-
  GND
  GND
  V+
  WaveOut
  +5V
  -5V
  A2AnalogOut
